# Fritzing sketch circuitDesign (saved by Fritzing 0.9.3b)
breadboards: 1

parts:
  U1 = NodeMCU V1.0
  Straight = LEDs [package=led10mm]
  Left = LEDs [package=led10mm]
  Right = LEDs [package=led10mm]
  U2 = RELAY-SOLIDSTATE [package=relay-s108t02]
  U3 = RELAY-SOLIDSTATE [package=relay-s108t02]
  U4 = RELAY-SOLIDSTATE [package=relay-s108t02]

nets:
  N1: U1.D0, U2.+
  N2: U1.D1, U3.+
  N3: U1.D2, U4.+
  N4: U1.GND, U2.-, U3.-, U4.-
  N5: Straight.C, U2.T1
  N6: Straight.A, Left.A, Right.A
  N7: Left.C, U3.T1
  N8: Right.C, U4.T1
  N9: U2.T2, U3.T2, U4.T2

custom parts:
  NodeMCU V1.0: ESP8266 based NodeMCU
